// Logisim project Controleur.circ as structural Verilog: 1 circuit, main circuit main
module main (
  input  [15:0] Instructions,
  input  Clock,
  input  Reset,
  output [7:0] Program_Counter,
  output _0_Load__1_Store,
  output [3:0] Codop_de_l_ALU,
  output [2:0] Registre_Rm,
  output [2:0] Registre_Rd,
  output [2:0] Registre_Rn,
  output [7:0] Immediat_sur_8_bits,
  output [4:0] Imm5
);


  // Other names for the same wires on the sheet: Clk = Clock; Codop[3:0] = Codop_de_l_ALU;
  //   Imm8[7:0] = Immediat_sur_8_bits; Instr[15:0] = Instructions; Load_Store = _0_Load__1_Store;
  //   PC[7:0] = Program_Counter; Rd[2:0] = Registre_Rd; Rm[2:0] = Registre_Rm; Rn[2:0] = Registre_Rn

  // Notes on the sheet:
  //   INPUTS
  //   OUTPUTS
endmodule
