// Logisim project Projet_PEP.circ as structural Verilog: 1 circuit, main circuit main
module main (
  input  CarryIn,
  input  [4:0] Shifter,
  input  [3:0] CodeOp,
  input  [31:0] DataIn,
  input  in_5,
  input  [2:0] RegA,
  input  [2:0] RegB,
  input  [2:0] RegDest,
  output [3:0] out_9
);

  wire button_1_out, button_2_out;
  wire [31:0] alu_32_bits_1_out_6, banc_registre_1_p4, banc_registre_1_p6, multiplexer_1_out;

  Button button_1 (.out(button_1_out));
  Button button_2 (.out(button_2_out));
  Multiplexer #(.width(32), .enable("false")) multiplexer_1 (
    .in0(alu_32_bits_1_out_6), .in1(DataIn), .out(multiplexer_1_out), .sel(in_5));
  // Banc_registre banc_registre_1: pin names not known; wires that end beside it: button_2_out, button_1_out, RegDest, banc_registre_1_p4, multiplexer_1_out, banc_registre_1_p6, RegB, RegA
  ALU_32_Bits alu_32_bits_1 (
    .CarryIn(CarryIn), .Shifter(Shifter), .A(banc_registre_1_p6), .B(banc_registre_1_p4), .CodeOp(CodeOp),
    .Flags(out_9), .out_6(alu_32_bits_1_out_6));
endmodule
